# Fritzing sketch ESP32_A2DP (saved by Fritzing 1.0.1rc)
breadboards: 1

parts:
  U1 = ESP32-38PinWide [part_number=ESP32-38PinWide]
  U2 = 3.5mm Audio Jack [package=audio-jack-3.5mm-smd]
  R1 = Resistor [tolerance=±5% power=0.25W resistance=1k package=THT]
  R2 = Resistor [tolerance=±5% power=0.25W resistance=1k package=THT]
  R3 = Resistor [tolerance=±5% power=0.25W resistance=100 package=THT]
  R4 = Resistor [tolerance=±5% power=0.25W resistance=100 package=THT]
  C1 = Ceramic Capacitor [capacitance=0.1µF voltage=35V package="100 mil [THT, multilayer]"]
  C2 = Ceramic Capacitor [capacitance=0.1µF voltage=35V package="100 mil [THT, multilayer]"]

nets:
  N1: U1.GPIO25, R1.Pin_1
  N2: U1.GPIO26, R2.Pin_1
  N3: U1.GND, U2.SLEEVE, R3.Pin_0, R4.Pin_0
  N4: U2.RIGHT, C1.0
  N5: U2.LEFT, C2.0
  N6: R1.Pin_0, R3.Pin_1, C2.1
  N7: R2.Pin_0, R4.Pin_1, C1.1

custom parts:
  ESP32-38PinWide: Generic 38-Pin ESP32 with wide format (only access to one side of pins on a breadboard) based on Stephen Lilley's HiLetgo ESP-WROOM-32 ESP32 ESP-32S Development Board.
